# Fritzing sketch Receptor_Infrarrojo (saved by Fritzing 0.9.3b)
breadboards: 1

parts:
  IR1 = TSOP312.., 314.. [package=THT]
  Componente1 = Arduino Uno (Rev3)
  LED1 = LED - 5mm [color="Orange (620nm)" package="5 mm [THT]"]

nets:
  N1: IR1.GND, Componente1.D11_PWM/MOSI
  N2: IR1.Data, Componente1.5V
  N3: Componente1.D13/SCK, LED1.anode
